# Fritzing sketch Board_Layout (saved by Fritzing 0.9.3b)
perfboards: 1

parts:
  Pololu_A1 = Pololu A4988 [package=SO16]
  J1 = Power Jack [package=power_jack_pth]
  C1 = Capacitor Polarized [part_number=100 package=cpol-radial-100uf-25v]
  J2 = female pin header, 8 pins [form="♀ (female)"]
  J3 = female pin header, 8 pins [form="♀ (female)"]
  J4 = male pin header, 4 pins [form="♂ (male)"]
  J5 = female pin header, 8 pins [form="♀ (female)"]
  J6 = female pin header, 8 pins [form="♀ (female)"]
  J7 = male pin header, 4 pins [form="♂ (male)"]
  C2 = Capacitor Polarized [part_number=100 package=cpol-radial-100uf-25v]
  Pololu_A3 = Pololu A4988 [package=SO16]
  J9 = male pin header, 2 pins [form="♂ (male)"]
  J10 = male pin header, 2 pins [form="♂ (male)"]
  J11 = male pin header, 2 pins [form="♂ (male)"]
  J12 = male pin header, 3 pins [form="♂ (male)"]
  J13 = male pin header, 3 pins [form="♂ (male)"]
  J14 = male pin header, 3 pins [form="♂ (male)"]
  J15 = male pin header, 3 pins [form="♂ (male)"]

nets:
  N1: Pololu_A1.ENABLE, J2.pin1
  N2: Pololu_A1.MS1, J2.pin2, J12.pin1
  N3: Pololu_A1.MS2, J2.pin3, J12.pin2
  N4: Pololu_A1.MS3, J2.pin4, J12.pin3
  N5: Pololu_A1.RESET, Pololu_A1.SLEEP, J2.pin5, J2.pin6
  N6: Pololu_A1.STEP, J2.pin7, J10.pin1
  N7: Pololu_A1.DIR, J2.pin8, J10.pin2
  N8: Pololu_A1.GND#8, J3.pin8, J6.pin8, Pololu_A3.GND#8, J9.pin2
  VDD: Pololu_A1.VDD, J3.pin7, J6.pin7, Pololu_A3.VDD, J9.pin1, J14.pin1, J14.pin2, J14.pin3, J15.pin1, J15.pin2, J15.pin3
  N9: Pololu_A1.1B, J3.pin6, J4.pin4
  N10: Pololu_A1.1A, J3.pin5, J4.pin3
  N11: Pololu_A1.2A, J3.pin4, J4.pin2
  N12: Pololu_A1.2B, J3.pin3, J4.pin1
  N13: Pololu_A1.GND#14, J1.GNDBREAK, C1.-, J3.pin2, J6.pin2, C2.-, Pololu_A3.GND#14
  N14: Pololu_A1.VMOT, J1.PWR, C1.+, J3.pin1, J6.pin1, C2.+, Pololu_A3.VMOT
  N15: J5.pin1, Pololu_A3.ENABLE
  N16: J5.pin2, Pololu_A3.MS1, J13.pin1
  N17: J5.pin3, Pololu_A3.MS2, J13.pin2
  N18: J5.pin4, Pololu_A3.MS3, J13.pin3
  N19: J5.pin5, J5.pin6, Pololu_A3.RESET, Pololu_A3.SLEEP
  N20: J5.pin7, Pololu_A3.STEP, J11.pin1
  N21: J5.pin8, Pololu_A3.DIR, J11.pin2
  N22: J6.pin3, J7.pin1, Pololu_A3.2B
  N23: J6.pin4, J7.pin2, Pololu_A3.2A
  N24: J6.pin5, J7.pin3, Pololu_A3.1A
  N25: J6.pin6, J7.pin4, Pololu_A3.1B
